// Logisim project 74LS379.circ as structural Verilog: 1 circuit, main circuit 74LS379
module _74LS379 (
  input  CLK,
  input  _1D,
  input  _2D,
  input  _3D,
  input  _4D,
  input  nG,
  output _1Q,
  output _2Q,
  output _3Q,
  output _4Q
);

  wire not_1_out;

  not not_1 (not_1_out, nG);
  D_Flip_Flop Rise (.clk(CLK), .D(_1D), .Q(_1Q), .en(not_1_out));  // open: Qn, preset, reset
  D_Flip_Flop Rise_2 (.clk(CLK), .D(_2D), .Q(_2Q), .en(not_1_out));  // open: Qn, preset, reset
  D_Flip_Flop Rise_3 (.clk(CLK), .D(_3D), .Q(_3Q), .en(not_1_out));  // open: Qn, preset, reset
  D_Flip_Flop Rise_4 (.clk(CLK), .D(_4D), .Q(_4Q), .en(not_1_out));  // open: Qn, preset, reset

  // Notes on the sheet:
  //   74LS379
endmodule
