// Logisim project 74LS68.circ as structural Verilog: 1 circuit, main circuit 74LS68
module _74LS68 (
  input  _1J,
  input  _1CLOCK,
  input  _1K,
  input  _1_CLEAR,
  input  _2J,
  input  _2CLOCK,
  input  _2K,
  input  _2_CLEAR,
  output _1Q,
  output _1_Q,
  output _2Q,
  output _2_Q
);

  wire not_1_out, not_2_out;

  not not_1 (not_1_out, _1_CLEAR);
  not not_2 (not_2_out, _2_CLEAR);
  J_K_Flip_Flop j_k_ff_1 (.J(_1J), .clk(_1CLOCK), .K(_1K), .Q(_1Q), .Qn(_1_Q), .reset(not_1_out));  // open: preset, en
  J_K_Flip_Flop j_k_ff_2 (.J(_2J), .clk(_2CLOCK), .K(_2K), .Q(_2Q), .Qn(_2_Q), .reset(not_2_out));  // open: preset, en

  // Notes on the sheet:
  //   74LS68
endmodule
